# Fritzing sketch SnakeRobot_V1 (saved by Fritzing 0.9.0b)

parts:
  Part1 = Arduino Pro Mini v13  # not connected
  U1 = LIPO-1000mAh [package=lipo-1000]
  12V = LIPO-1000mAh [package=lipo-1000]
  5V_regulator = Voltage Regulator - 5V [package="TO220 [THT]"]
  Part5 = Arduino Pro Mini v13
  J17 = Basic Servo
  J19 = Basic Servo
  J20 = Basic Servo
  5V_regulator_2 = Voltage Regulator - 5V [package="TO220 [THT]"]
  J18 = Basic Servo
  Part6 = Arduino Pro Mini v13
  J21 = Basic Servo
  J22 = Basic Servo
  J23 = Basic Servo
  J24 = Basic Servo
  U11 = LIPO-1000mAh [package=lipo-1000]
  5V_regulator_3 = Voltage Regulator - 5V [package="TO220 [THT]"]
  Part7 = Arduino Pro Mini v13
  J25 = Basic Servo
  J26 = Basic Servo
  J27 = Basic Servo
  J28 = Basic Servo
  U13 = LIPO-1000mAh [package=lipo-1000]
  5V_regulator_4 = Voltage Regulator - 5V [package="TO220 [THT]"]
  Part8 = Arduino Pro Mini v13
  J29 = Basic Servo
  J30 = Basic Servo
  J31 = Basic Servo
  J32 = Basic Servo
  U15 = LIPO-1000mAh [package=lipo-1000]
  5V_regulator_5 = Voltage Regulator - 5V [package="TO220 [THT]"]
  Pull_Up_Resistor = Resistor [tolerance=±5% resistance=10 package=THT]  # not connected

nets:
  N1: U1.+, 5V_regulator_2.input_voltage
  GND: U1.-, Part5.RAW, Part5.GND, J20.gnd, 5V_regulator_2.GND
  N2: 12V.+, 5V_regulator.input_voltage
  N3: 12V.-, 5V_regulator.GND
  N4: Part5.RESET, Part5.VCC, 5V_regulator_2.output_voltage
  N5: Part5.A0, Part5.D13/SCK, J20.pulse
  N6: Part5.D12/MISO, J19.pulse
  N7: Part5.D11_PWM/MOSI, J18.pulse
  N8: Part5.D10_PWM/SS, J17.pulse
  GND_2: Part6.GND, Part6.RESET, J22.gnd, U11.-, 5V_regulator_3.GND
  VCC: Part6.VCC, Part6.A3, J22.vcc, 5V_regulator_3.output_voltage
  N9: Part6.D13/SCK, J22.pulse
  N10: Part6.D12/MISO, J21.pulse
  N11: Part6.D11_PWM/MOSI, J24.pulse
  N12: Part6.D10_PWM/SS, J23.pulse
  N13: U11.+, 5V_regulator_3.input_voltage
  GND_3: Part7.GND, J28.gnd, U13.-, 5V_regulator_4.GND
  VCC_2: Part7.VCC, J28.vcc, 5V_regulator_4.output_voltage
  N14: Part7.D13/SCK, J28.pulse
  N15: Part7.D12/MISO, J27.pulse
  N16: Part7.D11_PWM/MOSI, J25.pulse
  N17: Part7.D10_PWM/SS, J26.pulse
  N18: U13.+, 5V_regulator_4.input_voltage
  GND_4: Part8.GND, J29.gnd, U15.-, 5V_regulator_5.GND
  VCC_3: Part8.VCC, J29.vcc, 5V_regulator_5.output_voltage
  N19: Part8.D13/SCK, J29.pulse
  N20: Part8.D12/MISO, J32.pulse
  N21: Part8.D11_PWM/MOSI, J31.pulse
  N22: Part8.D10_PWM/SS, J30.pulse
  N23: U15.+, 5V_regulator_5.input_voltage

notes:
  IP Camera (Wifi)
  PS2 Receiver
  DATA(Pink),
  CMD(Blue), CLK(Green), ATT(Orange),
  VCC,
  GND
  Master Module
  Slave Module
